# Fritzing sketch nai_circuit_diagram (saved by Fritzing 0.7.10b)
breadboards: 1

parts:
  IC1 = IC, DIP package, 24 pins [chip_label=max7219]
  R1 = Resistor [tolerance=±5% resistance=47 package=THT]
  C1 = Electrolytic Capacitor [capacitance=10µF package="100 mil [THT, electrolytic]"]
  C2 = Tantalum Capacitor [capacitance=100nF package="100 mil [THT, tantalum]"]
  J1 = female pin header, 2 pins [form="♀ (female)"]
  J2 = female pin header, 2 pins [form="♀ (female)"]
  J3 = female pin header, 2 pins [form="♀ (female)"]
  R2 = Resistor [tolerance=±5% resistance=220 package=THT]
  LED1 = LED - 5mm [color="Red (633nm)" package="5 mm [THT]"]
  J4 = female pin header, 2 pins [form="♀ (female)"]  # not connected
  J5 = female pin header, 2 pins [form="♀ (female)"]  # not connected
  J6 = female pin header, 2 pins [form="♀ (female)"]  # not connected
  J7 = female pin header, 2 pins [form="♀ (female)"]  # not connected
  J8 = female pin header, 2 pins [form="♀ (female)"]  # not connected
  J9 = female pin header, 2 pins [form="♀ (female)"]  # not connected

nets:
  N1: IC1.pin1, J3.pin1
  N2: IC1.pin4, IC1.pin9, C1.-, C2.-, J2.pin1, LED1.cathode
  N3: IC1.pin12, J1.pin2
  N4: IC1.pin13, J3.pin2
  N5: IC1.pin18, R1.Pin_0
  N6: IC1.pin19, R1.Pin_1, C1.+, C2.+, J2.pin2
  N7: J1.pin1, R2.Pin_1
  N8: R2.Pin_0, LED1.anode
